# Fritzing sketch raspberry_pi_7_segment_display (saved by Fritzing 0.9.3b)
breadboards: 2

parts:
  Raspberry_Pi_1 = Raspberry Pi 3 [part_number=RPI-3-V1.2]
  LED1 = 7-SEGMENT-4DIGIT-YOUNGSUN [package=7-segment-4digit-youngsun-longpads]
  Raspberry_Pi_Zero1 = Raspberry Pi Zero  # not connected
  R2 = Resistor [tolerance=±5% resistance=100 package="0402 [SMD]"]
  R3 = Resistor [tolerance=±5% resistance=100 package="0402 [SMD]"]
  R6 = Resistor [tolerance=±5% resistance=100 package="0402 [SMD]"]
  R7 = Resistor [tolerance=±5% resistance=100 package="0402 [SMD]"]
  R8 = Resistor [tolerance=±5% resistance=100 package="0402 [SMD]"]
  R9 = Resistor [tolerance=±5% resistance=100 package="0402 [SMD]"]
  R10 = Resistor [tolerance=±5% resistance=100 package="0402 [SMD]"]

nets:
  N1: Raspberry_Pi_1.GIPO17, R2.Pin_0
  N2: Raspberry_Pi_1.GIPO27, R3.Pin_0
  N3: Raspberry_Pi_1.GIPO22, R6.Pin_0
  N4: Raspberry_Pi_1.GIPO5, R10.Pin_1
  N5: Raspberry_Pi_1.GIPO6, R9.Pin_1
  N6: Raspberry_Pi_1.GIPO13, R8.Pin_1
  N7: Raspberry_Pi_1.GIPO19, R7.Pin_1
  N8: Raspberry_Pi_1.GND, LED1.DIG3
  N9: LED1.DIG1, R7.Pin_0
  N10: LED1.DIG2, R8.Pin_0
  N11: LED1.COL-A, R9.Pin_0
  N12: LED1.E, R10.Pin_0
  N13: LED1.F, R6.Pin_1
  N14: LED1.A, R3.Pin_1
  N15: LED1.G, R2.Pin_1
